# Fritzing sketch Circuit (saved by Fritzing 0.9.0b)
breadboards: 1

parts:
  L1 = Inductor [package="1206 [SMD]"]
  L2 = Inductor [package="1206 [SMD]"]
  Multiplieur = IC, DIP package, 8 pins [chip_label=X]
  R3 = Resistor [tolerance=±5% resistance=470 package=THT]
  C1 = Ceramic Capacitor [capacitance=10nF package="100 mil [THT, multilayer]"]
  R4 = Resistor [tolerance=±5% resistance=560k package=THT]
  R5 = Resistor [tolerance=±5% resistance=2.2k package=THT]
  Comparateur_1 = OPA344 [package=sot23-5]
  C2 = Ceramic Capacitor [capacitance=1µF package="100 mil [THT, multilayer]"]
  R6 = Resistor [tolerance=±5% resistance=470k package=THT]
  TP1 = TEST-POINT [package=pad.03x.05]
  TP2 = TEST-POINT [package=pad.03x.05]
  TP3 = TEST-POINT [package=pad.03x.05]
  R7 = Resistor [tolerance=±5% resistance=680k package=THT]
  R8 = Resistor [tolerance=±5% resistance=330k package=THT]
  TP4 = TEST-POINT [package=pad.03x.05]
  Sortie = Header 1 [package=luxeon-pad]
  Entrée = Header 1 [package=luxeon-pad]
  TP5 = TEST-POINT [package=pad.03x.05]
  Amplificateur_non_inverseur_1 = OPA344 [package=sot23-5]
  D1 = Rectifier Diode [part_number=1N4001 package="300 mil [THT]"]

nets:
  N1: L1.pin_0, Multiplieur.pin3, Entrée.1
  GND: L1.pin_1, L2.pin_1, Multiplieur.pin2, Multiplieur.pin4, Multiplieur.pin6, R5.Pin_0, C2.1, R8.Pin_1, D1.cathode
  N2: L2.pin_0, Multiplieur.pin1, TP5.1
  N3: Multiplieur.pin7, R3.Pin_0
  N4: R3.Pin_1, C1.1, TP2.1, Amplificateur_non_inverseur_1.+IN
  N5: R4.Pin_0, R5.Pin_1, Amplificateur_non_inverseur_1.-IN
  N6: R4.Pin_1, Comparateur_1.+IN, R6.Pin_0, TP3.1, Amplificateur_non_inverseur_1.OUT
  N7: Comparateur_1.OUT, R7.Pin_0, TP4.1
  -15V: Comparateur_1.V-, Amplificateur_non_inverseur_1.V-
  N8: Comparateur_1.-IN, C2.0, R6.Pin_1
  15V: Comparateur_1.V+, Amplificateur_non_inverseur_1.V+
  N9: TP1.1, R7.Pin_1, R8.Pin_0, Sortie.1, D1.anode
